# Fritzing sketch ada_pi (saved by Fritzing 0.9.3b)

parts:
  Part1 = Adafruit Feather 32u4 Bluefruit [part_number="Adafruit #2829"]
  Raspberry_Pi_Zero1 = Raspberry Pi Zero

nets:
  N1: Part1.MISO, Raspberry_Pi_Zero1.GPIO18
  N2: Part1.MOSI, Raspberry_Pi_Zero1.GPIO23
  N3: Part1.SCK, Raspberry_Pi_Zero1.GPIO24
  N4: Part1.GND, Raspberry_Pi_Zero1.GPIO14
  N5: Part1.RST, Raspberry_Pi_Zero1.GPIO12
  N6: Part1.VBUS, Raspberry_Pi_Zero1.5V

notes:
  Based on Info from Here

custom parts:
  Adafruit Feather 32u4 Bluefruit: This is the Adafruit Feather 32u4 Bluefruit - our take on an 'all-in-one' Arduino-compatible + Bluetooth Low Energy with built in USB and battery charging. Its an Adafruit Feather 32u4 with a BTLE module, ready to rock! We have other boards in the Feather family, check'em out here. Bluetooth Low Energy is the hottest new low-power, 2.4GHz spectrum wireless protocol. In particular, its the only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
