# Fritzing sketch ada_pi_magpi61 (saved by Fritzing 0.9.3b)

parts:
  Part1 = Adafruit Feather 32u4 Bluefruit [part_number="Adafruit #2829"]
  Raspberry_Pi_Zero1 = Raspberry Pi Zero
  PIR1 = PIR sensor
  R2 = Resistor [tolerance=±5% resistance=220 package="0805 [SMD]"]
  LED1 = LEDs [package=led10mm]
  R3 = Resistor [tolerance=±5% resistance=220 package="0805 [SMD]"]
  LED2 = LEDs [package=led10mm]

nets:
  N1: Part1.1/TX, Raspberry_Pi_Zero1.GPIO15
  N2: Part1.0/RX, Raspberry_Pi_Zero1.GPIO14
  N3: Part1.MISO, Raspberry_Pi_Zero1.GPIO18
  N4: Part1.MOSI, Raspberry_Pi_Zero1.GPIO23
  N5: Part1.SCK, Raspberry_Pi_Zero1.GPIO24
  GND: Part1.GND, Raspberry_Pi_Zero1.GND, PIR1.GND, LED1.C, LED2.C
  N6: Part1.RST, Raspberry_Pi_Zero1.GPIO12
  5V: Part1.VBUS, Raspberry_Pi_Zero1.5V, PIR1.VDD
  N7: Part1.3, PIR1.SIG
  N8: R2.Pin_1, LED2.A
  N9: LED1.A, R3.Pin_1

notes:
  Based on Info from Here

custom parts:
  Adafruit Feather 32u4 Bluefruit: This is the Adafruit Feather 32u4 Bluefruit - our take on an 'all-in-one' Arduino-compatible + Bluetooth Low Energy with built in USB and battery charging. Its an Adafruit Feather 32u4 with a BTLE module, ready to rock! We have other boards in the Feather family, check'em out here. Bluetooth Low Energy is the hottest new low-power, 2.4GHz spectrum wireless protocol. In particular, its the only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
